# Fritzing sketch TSFRL_master_module (saved by Fritzing 0.9.0b)
perfboards: 2

parts:
  keyLeft = Pushbutton [package="[THT]"]
  LED1 = LED - 3mm [color="Red (633nm)" package="3 mm [THT]"]  # not connected
  J1 = female pin header, 2 pins [form="♀ (female)"]  # not connected
  keyUp = Pushbutton [package="[THT]"]
  keyStart = Pushbutton [package="[THT]"]
  IC1 = Hex Inverter Schmitt Trigger SN74HC14 [package="DIP (Dual Inline)"]  # not connected
  keyRight = Pushbutton [package="[THT]"]
  keyReset = Pushbutton [package="[THT]"]
  keyDown = Pushbutton [package="[THT]"]
  J2 = single row smd male pin header, 11 pins [form="♂ (male)"]

nets (from the breadboard view):
  N1: keyLeft.Pin_1, keyLeft.Pin_2
  N2: keyLeft.Pin_3, keyLeft.Pin_4, J2.pin5
  N3: keyUp.Pin_1, keyUp.Pin_2
  N4: keyUp.Pin_3, keyUp.Pin_4, J2.pin7
  N5: keyStart.Pin_1, keyStart.Pin_2, J2.pin4
  N6: keyStart.Pin_3, keyStart.Pin_4, keyReset.Pin_1, keyReset.Pin_2, J2.pin2
  N7: keyRight.Pin_1, keyRight.Pin_2
  N8: keyRight.Pin_3, keyRight.Pin_4, J2.pin6
  N9: keyReset.Pin_3, keyReset.Pin_4
  N10: keyDown.Pin_1, keyDown.Pin_2
  N11: keyDown.Pin_3, keyDown.Pin_4, J2.pin3
